# Fritzing sketch Circuit (saved by Fritzing 0.9.5d)

parts:
  WeMos_D1_Mini1 = WeMos D1 Mini
  Part1 = NeoPixel Stick [part_number=1426]
  S1 = Pushbutton [package="[SMD]"]
  S2 = Pushbutton [package="[SMD]"]
  S3 = Pushbutton [package="[SMD]"]
  S4 = Pushbutton [package="[SMD]"]
  OLED1 = OLED 128x64 I2C Monochrome Display

nets:
  3V3: WeMos_D1_Mini1.3V3, OLED1.VDD
  5V: WeMos_D1_Mini1.5V, Part1.+5V
  N1: WeMos_D1_Mini1.D1, OLED1.SCK
  N2: WeMos_D1_Mini1.D2, OLED1.SDA
  N3: WeMos_D1_Mini1.D3, Part1.DATAIN
  N4: WeMos_D1_Mini1.D4, S1.Pin_1, S1.Pin_2
  N5: WeMos_D1_Mini1.D5, S4.Pin_1
  N6: WeMos_D1_Mini1.D6, S3.Pin_1, S3.Pin_2
  N7: WeMos_D1_Mini1.D7, S2.Pin_1, S2.Pin_2
  GND: WeMos_D1_Mini1.G, Part1.GND, S1.Pin_3, S1.Pin_4, S2.Pin_3, S2.Pin_4, S3.Pin_3, S4.Pin_3, S4.Pin_4, OLED1.GND

custom parts:
  NeoPixel Stick: Make your own little LED strip arrangement with this stick of NeoPixel LEDs. We crammed 8 of the tiny 5050 (5mm x 5mm) smart RGB LEDs onto a PCB with mounting holes and a chainable design. Use only one microcontroller pin to control as many as you can chain together! Each LED is addressable as the driver chip is inside the LED. Each one has ~18mA constant current drive so the color will be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
